# Fritzing sketch numero1-2 (saved by Fritzing 0.9.8b)
breadboards: 1

parts:
  LED1 = smd LED [color="Red (633nm)" package="0805 [SMD]"]
  R1 = Resistor [tolerance=±5% resistance=220 package="0805 [SMD]"]
  VCC1 = Battery

nets:
  N1: LED1.cathode, LED1.anode, R1.Pin_0, R1.Pin_1, VCC1.-, VCC1.+
