# Fritzing sketch numero2 (saved by Fritzing 0.9.8b)
breadboards: 1

parts:
  LED1 = smd LED [color="Red (633nm)" package="0805 [SMD]"]
  R1 = Resistor [tolerance=±5% resistance=220 package="0805 [SMD]"]
  VCC1 = Battery
  LED2 = smd LED [color="Red (633nm)" package="0805 [SMD]"]
  LED3 = smd LED [color="Red (633nm)" package="0805 [SMD]"]
  LED4 = smd LED [color="Red (633nm)" package="0805 [SMD]"]

nets:
  N1: LED1.cathode, VCC1.-, LED2.cathode, LED3.cathode, LED4.cathode
  N2: LED1.anode, R1.Pin_1, LED2.anode, LED3.anode, LED4.anode
  N3: R1.Pin_0, VCC1.+
