# Fritzing sketch numero3 (saved by Fritzing 0.9.8b)
breadboards: 1

parts:
  VCC1 = Battery
  Part1 = LilyPad Buzzer
  LED1 = smd LED [color="Red (633nm)" package="1206 [SMD]"]
  R1 = Resistor [tolerance=±5% resistance=220 package="1206 [SMD]"]

nets:
  N1: VCC1.-, Part1.-, R1.Pin_1
  N2: VCC1.+, Part1.+, LED1.anode
  N3: LED1.cathode, R1.Pin_0
