# Fritzing sketch numero4 (saved by Fritzing 0.9.8b)
breadboards: 1

parts:
  VCC1 = Battery
  LED1 = smd LED [color="Red (633nm)" package="1206 [SMD]"]
  R1 = Resistor [tolerance=±5% resistance=220 package="1206 [SMD]"]
  Q1 = NPN-Transistor [package="TO92 [THT]"]

nets:
  N1: VCC1.-, Q1.C
  N2: VCC1.+, LED1.anode
  N3: LED1.cathode, R1.Pin_0
  N4: R1.Pin_1, Q1.E
