# Fritzing sketch numero5 (saved by Fritzing 0.9.8b)
breadboards: 1

parts:
  VCC1 = Battery
  LED1 = smd LED [color="Red (633nm)" package="1206 [SMD]"]
  R1 = Resistor [tolerance=±5% resistance=220 package="1206 [SMD]"]
  Q1 = NPN-Transistor [package="TO92 [THT]"]
  S2 = Pushbutton [package="[THT]"]
  R2 = Resistor [tolerance=±5% resistance=220 package="1206 [SMD]"]

nets:
  N1: VCC1.-, LED1.cathode
  N2: VCC1.+, S2.Pin_3, S2.Pin_4
  N3: LED1.anode, R2.Pin_1
  N4: R1.Pin_0, Q1.C, S2.Pin_1, S2.Pin_2
  N5: R1.Pin_1, Q1.B
  N6: Q1.E, R2.Pin_0
