# Fritzing sketch schema_1 (saved by Fritzing 0.9.8b)
breadboards: 1

parts:
  Raspberry_Pi_A1 = Raspberry Pi A
  SG1 = Buzzer 12mm [package=buzzer-cmt1603]
  LED1 = smd LED [color="Red (633nm)" package="0805 [SMD]"]
  LED2 = smd LED [color="Red (633nm)" package="0805 [SMD]"]
  LED3 = smd LED [color="Red (633nm)" package="0805 [SMD]"]
  LED4 = smd LED [color="Red (633nm)" package="0805 [SMD]"]
  LED5 = smd LED [color="Red (633nm)" package="0805 [SMD]"]
  LED6 = smd LED [color="Red (633nm)" package="0805 [SMD]"]
  LED7 = smd LED [color="Red (633nm)" package="0805 [SMD]"]
  LED8 = smd LED [color="Red (633nm)" package="0805 [SMD]"]
  R1 = Resistor [tolerance=±5% resistance=220 package="0402 [SMD]"]
  LED9 = RGB LED (com. anode, rbg) [package="5 mm [THT]"]
  R2 = Resistor [tolerance=±5% resistance=220 package="0402 [SMD]"]
  S1 = SPST Switch [package=switch-spdt-smd]

nets:
  N1: Raspberry_Pi_A1.3V3, R2.Pin_0
  N2: Raspberry_Pi_A1.GPIO_2, SG1.1
  N3: Raspberry_Pi_A1.GND, R1.Pin_1, S1.O
  N4: Raspberry_Pi_A1.GPIO_23, LED4.anode
  N5: Raspberry_Pi_A1.GPIO_17, LED7.anode
  N6: Raspberry_Pi_A1.GPIO_18, LED6.anode
  N7: Raspberry_Pi_A1.GPIO_27, LED1.anode
  N8: Raspberry_Pi_A1.GPIO_22, LED5.anode
  N9: Raspberry_Pi_A1.GPIO_4, LED8.anode
  N10: Raspberry_Pi_A1.GPIO_24, LED3.anode
  N11: Raspberry_Pi_A1.GPIO_25, LED2.anode
  N12: Raspberry_Pi_A1.GPIO_11, LED9.red_cathode
  N13: Raspberry_Pi_A1.GPIO_8, LED9.blue_cathode
  N14: Raspberry_Pi_A1.GPIO_7, LED9.green_cathode
  N15: SG1.2, S1.P
  N16: LED1.cathode, LED2.cathode, LED3.cathode, LED4.cathode, LED5.cathode, LED6.cathode, LED7.cathode, LED8.cathode, R1.Pin_0
  N17: LED9.common_anode, R2.Pin_1
