# Fritzing sketch ShemaTP3 (saved by Fritzing 0.9.8b)
breadboards: 1

parts:
  Buzzer = Buzzer 12mm [package=buzzer-ccv-kit]
  RGBLED = RGB LED (com. cathode, rgb) [package="5 mm [THT]"]
  Ultrasonic_Sensor = HC-SR04 Ultrasonic Distance Sensor
  J1 = Infrared Proximity Sensor
  R1 = Resistor [tolerance=±5% resistance=1k package="0603 [SMD]"]
  R2 = Resistor [tolerance=±5% resistance=1k package="0603 [SMD]"]
  RHT1 = Humidity and Temperature Sensor RHT03
  Raspberry_Pi1 = Raspberry Pi B+

nets:
  N1: Buzzer.1, Raspberry_Pi1.GPIO6
  GND: Buzzer.2, Ultrasonic_Sensor.GND, J1.GND, R2.Pin_1, RHT1.GND_1, Raspberry_Pi1.GND
  N2: RGBLED.red_anode, Raspberry_Pi1.GPIO13
  N3: RGBLED.common_cathode, Raspberry_Pi1.3v3
  N4: RGBLED.green_anode, Raspberry_Pi1.GPIO19
  N5: RGBLED.blue_anode, Raspberry_Pi1.GPIO26
  VCC: Ultrasonic_Sensor.VCC, J1.Vcc, RHT1.Vcc, Raspberry_Pi1.5V
  N6: Ultrasonic_Sensor.TRIG, Raspberry_Pi1.GPIO23
  N7: Ultrasonic_Sensor.ECHO, R1.Pin_0
  N8: J1.Vout, Raspberry_Pi1.GPIO25
  N9: R1.Pin_1, R2.Pin_0, Raspberry_Pi1.GPIO24
  N10: RHT1.Data-signal, Raspberry_Pi1.GPIO21
