# Fritzing sketch Schema (saved by Fritzing 0.9.8b)
breadboards: 1

parts:
  Raspberry_Pi1 = Raspberry Pi B+
  R1 = Resistor [tolerance=±5% resistance=220 package="0805 [SMD]"]
  R2 = Trimmer Potentiometer [maximum_resistance=10kΩ package=THT]
  D1 = LED_BARGRAPH_10 [package=led_bargaph_10]
  Part1 = Adafruit ADS1115 16Bit I2C ADC [part_number="Adafruit #1085"]
  R3 = Resistor [tolerance=±5% resistance=220 package="0805 [SMD]"]
  R4 = Resistor [tolerance=±5% resistance=220 package="0805 [SMD]"]
  R5 = Resistor [tolerance=±5% resistance=220 package="0805 [SMD]"]
  R6 = Resistor [tolerance=±5% resistance=220 package="0805 [SMD]"]
  R7 = Resistor [tolerance=±5% resistance=220 package="0805 [SMD]"]
  R8 = Resistor [tolerance=±5% resistance=220 package="0805 [SMD]"]
  R9 = Resistor [tolerance=±5% resistance=220 package="0805 [SMD]"]
  R10 = Resistor [tolerance=±5% resistance=220 package="0805 [SMD]"]
  R11 = Resistor [tolerance=±5% resistance=220 package="0805 [SMD]"]

nets:
  N1: Raspberry_Pi1.GPIO2, Part1.SDA
  N2: Raspberry_Pi1.GPIO3, Part1.SCL
  N3: Raspberry_Pi1.3V3, R2.leg2
  N4: Raspberry_Pi1.GPIO5, D1.A_A
  N5: Raspberry_Pi1.GPIO6, D1.B_A
  N6: Raspberry_Pi1.GPIO13, D1.C_A
  N7: Raspberry_Pi1.GPIO19, D1.D_A
  N8: Raspberry_Pi1.GPIO26, D1.E_A
  N9: Raspberry_Pi1.GND, R1.Pin_1, R2.leg1, R3.Pin_1, R4.Pin_1, R5.Pin_1, R6.Pin_1, R7.Pin_1, R8.Pin_1, R9.Pin_1, R10.Pin_1, R11.Pin_1
  N10: Raspberry_Pi1.GPIO25, D1.F_A
  N11: Raspberry_Pi1.GPIO24, D1.G_A
  N12: Raspberry_Pi1.GPIO23, D1.H_A
  N13: Raspberry_Pi1.GPIO18, D1.I_A
  N14: Raspberry_Pi1.GPIO15, D1.J_A
  5V: Raspberry_Pi1.5V, Part1.VDD
  N15: R1.Pin_0, D1.D_C
  N16: R2.wiper, Part1.ADDR
  N17: D1.J_C, R11.Pin_0
  N18: D1.I_C, R10.Pin_0
  N19: D1.H_C, R9.Pin_0
  N20: D1.G_C, R7.Pin_0
  N21: D1.F_C, R6.Pin_0
  N22: D1.E_C, R8.Pin_0
  N23: D1.C_C, R3.Pin_0
  N24: D1.B_C, R4.Pin_0
  N25: D1.A_C, R5.Pin_0

custom parts:
  Adafruit ADS1115 16Bit I2C ADC: For microcontrollers without an analog-to-digital converter or when you want a higher-precision ADC, the ADS1115 provides 16-bit precision at 860 samples/second over I2C. The chip can be configured as 4 single-ended input channels, or two differential channels. As a nice bonus, it even includes a programmable gain amplifier, up to x16, to help boost up smaller single/differential signals to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
