# Fritzing sketch ShemaTP3 (saved by Fritzing 0.9.8b)
breadboards: 1

parts:
  Raspberry_Pi1 = Raspberry Pi B+
  J1 = Basic Servo
  S1 = SWITCH-MOMENTARY-2 [package=tactile-pth]
  S2 = SWITCH-MOMENTARY-2 [package=tactile-pth]
  7_Segment2 = 7 Segment Display
  R1 = Resistor [tolerance=±5% resistance=220 package="1206 [SMD]"]
  R2 = Resistor [tolerance=±5% resistance=220 package="1206 [SMD]"]
  R3 = Resistor [tolerance=±5% resistance=220 package="1206 [SMD]"]
  R4 = Resistor [tolerance=±5% resistance=220 package="1206 [SMD]"]
  R5 = Resistor [tolerance=±5% resistance=220 package="1206 [SMD]"]
  R6 = Resistor [tolerance=±5% resistance=220 package="1206 [SMD]"]
  R8 = Resistor [tolerance=±5% resistance=220 package="1206 [SMD]"]
  R9 = Resistor [tolerance=±5% resistance=220 package="1206 [SMD]"]

nets:
  N1: Raspberry_Pi1.3v3, 7_Segment2.common_cathode
  N2: Raspberry_Pi1.GPIO2, R9.Pin_0
  N3: Raspberry_Pi1.GPIO3, R8.Pin_0
  N4: Raspberry_Pi1.GPIO4, R5.Pin_0
  GND: Raspberry_Pi1.GND, J1.gnd, S1.2, S2.2
  N5: Raspberry_Pi1.GPIO17, R1.Pin_0
  N6: Raspberry_Pi1.GPIO27, R4.Pin_0
  N7: Raspberry_Pi1.GPIO22, R3.Pin_0
  N8: Raspberry_Pi1.GPIO10, R2.Pin_0
  N9: Raspberry_Pi1.GPIO9, R6.Pin_0
  N10: Raspberry_Pi1.GPIO20, J1.pulse
  N11: Raspberry_Pi1.GPIO16, S1.1
  N12: Raspberry_Pi1.GPIO12, S2.1
  5V: Raspberry_Pi1.5V, J1.vcc
  N13: 7_Segment2.Segment_A#1, R8.Pin_1
  N14: 7_Segment2.Segment_F, R5.Pin_1
  N15: 7_Segment2.Segment_E, R1.Pin_1
  N16: 7_Segment2.Segment_D, R4.Pin_1
  N17: 7_Segment2.Segment_DP, R9.Pin_1
  N18: 7_Segment2.Segment_C, R3.Pin_1
  N19: 7_Segment2.Segment_B, R2.Pin_1
  N20: 7_Segment2.Segment_A#10, R6.Pin_1
