# Fritzing sketch ShemaTP3 (saved by Fritzing 0.9.8b)
breadboards: 1

parts:
  Raspberry_Pi1 = Raspberry Pi B+
  LED1 = smd LED [color="Red (633nm)" package="0805 [SMD]"]
  LED2 = RGB LED - (4 legs) [package="5 mm [THT]"]
  R1 = Resistor [tolerance=±5% resistance=220 package="0805 [SMD]"]
  Part1 = Adafruit ADS1115 16Bit I2C ADC [part_number="Adafruit #1085"]
  Potentiometre = Trimmer Potentiometer [maximum_resistance=10kΩ package=THT]
  R3 = Resistor [tolerance=±5% resistance=220 package="0805 [SMD]"]
  R4 = Resistor [tolerance=±5% resistance=220 package="0805 [SMD]"]
  R5 = Resistor [tolerance=±5% resistance=10000 package="0805 [SMD]"]
  R6 = Resistor [tolerance=±5% resistance=10000 package="0805 [SMD]"]
  LCD = LCD1602-I2C
  ThermoResistor = Temperature Sensor (Thermistor) [thermistor_type=NTC package=THT]
  Photoresistor = PHOTOCELL [package=photocell-kit]
  R11 = Resistor [tolerance=±5% resistance=220 package="0805 [SMD]"]

nets:
  3V3: Raspberry_Pi1.3v3, Raspberry_Pi1.3V3, Part1.VDD, Potentiometre.leg1, R5.Pin_0, R6.Pin_0
  N1: Raspberry_Pi1.GPIO2, Part1.SDA, LCD.SDA
  N2: Raspberry_Pi1.GPIO3, Part1.SCL, LCD.SCL
  GND: Raspberry_Pi1.GND, LED1.cathode, R1.Pin_1, Part1.GND, Potentiometre.leg2, R3.Pin_1, R4.Pin_1, LCD.GND, ThermoResistor.pin_0, Photoresistor.P$2
  N3: Raspberry_Pi1.GPIO21, R11.Pin_0
  N4: Raspberry_Pi1.GPIO16, LED2.common_anode
  N5: LED1.anode, R11.Pin_1
  N6: LED2.red_cathode, R3.Pin_0
  N7: LED2.green_cathode, R4.Pin_0
  N8: LED2.blue_cathode, R1.Pin_0
  N9: Part1.AIN2, R6.Pin_1, Photoresistor.P$1
  N10: Part1.AIN1, R5.Pin_1, ThermoResistor.pin_1
  N11: Part1.AIN0, Potentiometre.wiper

custom parts:
  Adafruit ADS1115 16Bit I2C ADC: For microcontrollers without an analog-to-digital converter or when you want a higher-precision ADC, the ADS1115 provides 16-bit precision at 860 samples/second over I2C. The chip can be configured as 4 single-ended input channels, or two differential channels. As a nice bonus, it even includes a programmable gain amplifier, up to x16, to help boost up smaller single/differential signals to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
  LCD1602-I2C: A standard character display, usually with 2x16 characters. Comes in many colors with LCM1602 IIC attached.
